# Fritzing sketch Gauge Meter (saved by Fritzing 0.9.4)

parts:
  U1 = ESP32-38PinWide [part_number=ESP32-38PinWide]
  LCD1 = TFT 1.8 inch 160x128 w SD
  R1 = Rotary Potentiometer (Small) [maximum_resistance=100kΩ package=THT]
  R2 = Resistor [tolerance=±5% resistance=1k package=THT]
  D1 = Zener Diode [part_number=1N4732A breakdown_voltage=3.3V package="300 mil [THT]"]
  U2 = LM2596-Step-Down-Converter [package=THT]

nets:
  N1: U1.GPIO35, R1.wiper, R2.Pin_0, D1.cathode
  N2: U1.GPIO11, LCD1.pin2, R1.leg1, D1.anode, U2.pin4
  N3: U1.VIN, LCD1.pin_1, R2.Pin_1, U2.pin3
  N4: U1.GPIO4, LCD1.pin4
  N5: U1.GPIO17, LCD1.pin_5
  N6: U1.GPIO5, LCD1.pin3
  N7: U1.GPIO18, LCD1.pin_7
  N8: U1.GPIO19, LCD1.pin_8
  N9: U1.GPIO23, LCD1.pin_6

notes:
  MISO
  SCK
  MOSI
  DC
  RST
  CS
  GND
  +5V
  1k
  ZPD 3.3
  180 Ohm
  5VDC
  12VDC
  Gauge Meter
  TFT Display
  Chipset: ILI9341
  Resolution: 320x240
  --------------

custom parts:
  ESP32-38PinWide: Generic 38-Pin ESP32 with wide format (only access to one side of pins on a breadboard) based on Stephen Lilley's HiLetgo ESP-WROOM-32 ESP32 ESP-32S Development Board.
  TFT 1.8 inch 160x128 w SD: This is a generic 1.8 tft spi lcd display available on ebay and others. The 1.8" display has 128x160 color pixels.
  LM2596-Step-Down-Converter: A dummy, proxy, ersatz, stand-in part for whatever you want. With 4 pins on a 100 mil inline pin header footprint.
